# Fritzing sketch RUNNING_TEXT (saved by Fritzing 0.9.3b)

parts:
  U1 = ESP 32 DEVKIT DOIT
  Part1 = Matrix LED de 8x8 basada en MAX7219

nets:
  N1: U1.D22, U1.D15, Part1.CS
  VIN: U1.VIN, Part1.VCC
  GND: U1.GND, Part1.GND
  N2: U1.D12, Part1.DIN
  N3: U1.D14, Part1.CLK
